# Fritzing sketch TrafficLight-Schematic (saved by Fritzing 0.9.10b)
breadboards: 1

parts:
  LED2 = LED - 3mm [color="Red (633nm)" current=0.030 package="3 mm [THT]"]
  LED3 = LED - 3mm [color="Yellow (595nm)" current=0.030 package="3 mm [THT]"]
  LED4 = LED - 3mm [color="Green (565nm)" current=0.030 package="3 mm [THT]"]
  LED5 = LED - 3mm [color="Red (633nm)" current=0.030 package="3 mm [THT]"]
  LED6 = LED - 3mm [color="Yellow (595nm)" current=0.030 package="3 mm [THT]"]
  LED7 = LED - 3mm [color="Green (565nm)" current=0.030 package="3 mm [THT]"]
  R1 = Resistor [tolerance=±5% power=0.25 resistance=220 package=THT]
  R2 = Resistor [tolerance=±5% power=0.25 resistance=220 package=THT]
  R3 = Resistor [tolerance=±5% power=0.25 resistance=220 package=THT]
  R4 = Resistor [tolerance=±5% power=0.25 resistance=220 package=THT]
  R5 = Resistor [tolerance=±5% power=0.25 resistance=220 package=THT]
  R6 = Resistor [tolerance=±5% power=0.25 resistance=220 package=THT]
  Part1 = Arduino Uno (Rev3)

nets:
  N1: LED2.cathode, Part1.D7
  N2: LED2.anode, R3.Pin_0
  N3: LED3.cathode, Part1.D6_PWM
  N4: LED3.anode, R2.Pin_0
  N5: LED4.cathode, Part1.D5_PWM
  N6: LED4.anode, R1.Pin_0
  N7: LED5.cathode, Part1.D8
  N8: LED5.anode, R4.Pin_0
  N9: LED6.cathode, Part1.D9_PWM
  N10: LED6.anode, R5.Pin_0
  N11: LED7.cathode, Part1.D10_PWM/SS
  N12: LED7.anode, R6.Pin_0
  N13: R1.Pin_1, R2.Pin_1, R3.Pin_1, R4.Pin_1, R5.Pin_1, R6.Pin_1, Part1.GND
